# Fritzing sketch arduino-thermostat (saved by Fritzing 0.9.3b)
breadboards: 1

parts:
  Part1 = Arduino Uno (Rev3)
  LCD1 = LCD screen
  R2 = Rotary Potentiometer (Small) [maximum_resistance=100kΩ package=THT]
  U1 = mystery part, 3 pins [chip_label=Temp°]
  S1 = Pushbutton [package="[THT]"]
  S2 = Pushbutton [package="[THT]"]
  S3 = Pushbutton [package="[THT]"]
  R3 = Resistor [tolerance=±5% resistance=10k package=THT]
  R4 = Resistor [tolerance=±5% resistance=10k package=THT]
  R5 = Resistor [tolerance=±5% resistance=10k package=THT]
  Relay_5V1 = Keyes Relay [package=THT]
  Relay_5V2 = Keyes Relay [package=THT]

nets:
  N1: Part1.A0, U1.pin1
  N2: Part1.D8, S2.Pin_1, S2.Pin_2, R4.Pin_1
  N3: Part1.D9_PWM, S1.Pin_1, S1.Pin_2, R3.Pin_1
  N4: Part1.D10_PWM/SS, Relay_5V1.signal
  N5: Part1.D11_PWM/MOSI, LCD1.RS
  N6: Part1.D12/MISO, LCD1.E
  N7: Part1.D13/SCK, Relay_5V2.signal
  GND: Part1.GND, LCD1.VSS, LCD1.R/W, LCD1.LED-, R2.leg1, U1.pin3, S1.Pin_3, S1.Pin_4, S2.Pin_3, S2.Pin_4, S3.Pin_3, S3.Pin_4, Relay_5V1.ground, Relay_5V2.ground
  N8: Part1.D2, LCD1.DB4
  N9: Part1.D3_PWM, LCD1.DB5
  N10: Part1.D4, LCD1.DB6
  N11: Part1.D5_PWM, LCD1.DB7
  N12: Part1.D7, S3.Pin_1, S3.Pin_2, R5.Pin_1
  5V: Part1.5V, LCD1.VDD, LCD1.LED+, R2.leg2, U1.pin2, R3.Pin_0, R4.Pin_0, R5.Pin_0, Relay_5V1.power, Relay_5V2.power
  N13: LCD1.V0, R2.wiper

custom parts:
  Keyes Relay: The Keyes 5V relay module is suitable for SCM development, home appliance control. It uses a 5V~12V TIL control signal which can control DC / AC signal.
